# Fritzing sketch Motion Sensor With ESP8266 Scheme (saved by Fritzing 0.9.2b)

parts:
  Part1 = Arduino Uno (Rev3)
  U1 = ESP8266 WiFi Module [part_number=ESP8266]
  PIR1 = PIR sensor

nets:
  GND: Part1.GND, U1.GND, PIR1.GND
  N1: Part1.D0/RX, U1.TXD
  N2: Part1.D1/TX, U1.RXD, U1.GPIO_0
  N3: Part1.D3_PWM, PIR1.SIG
  3V3: Part1.3V3, U1.VCC, U1.RST, U1.CH_PD
  5V: Part1.5V, PIR1.VDD

custom parts:
  ESP8266 WiFi Module: Generic WiFi Module based on the ESP8266 with onboard PCB antenna and UART communications
