# Fritzing sketch Untitled Sketch (saved by Fritzing 0.9.2b)
breadboards: 1

parts:
  Part1 = Arduino Uno (Rev3)
  LED1 = RGB LED (com. cathode, rgb) [package="5 mm [THT]"]
  R1 = Resistor [tolerance=±5% resistance=220 package=THT]
  VCC1 = Battery block 9V
  J1 = Piezo Speaker

nets:
  N1: Part1.D10_PWM/SS, J1.pin2
  N2: Part1.D11_PWM/MOSI, LED1.red_anode
  N3: Part1.D12/MISO, LED1.green_anode
  N4: Part1.D13/SCK, LED1.blue_anode
  N5: Part1.GND, R1.Pin_0, VCC1.-, J1.pin1
  N6: Part1.VIN, VCC1.+
